# Fritzing sketch Reciver (saved by Fritzing 0.9.3b)
breadboards: 1

parts:
  Part1 = Arduino Nano (Rev3.0)
  Part2 = NRF24L01+ Breakout Board
  METER1 = 7-Segment Panel Ammeter

nets:
  N1: Part1.RESET, METER1.GND
  GND: Part1.GND, Part2.GND
  N2: Part1.D2, METER1.CLK
  N3: Part1.D3, METER1.DIO
  N4: Part1.D7, Part2.CE
  N5: Part1.D8, Part2.CS
  N6: Part1.D11/MOSI, Part2.MOSI
  N7: Part1.D12/MISO, Part2.MISO
  5V: Part1.5V, METER1.VCC
  3V3: Part1.3V3, Part2.VCC
  N8: Part1.D13/SCK, Part2.SCK

custom parts:
  7-Segment Panel Ammeter: 7-Segment Panel Ammeter (0 to 9.99A)
