# Fritzing sketch Untitled Sketch 2 (saved by Fritzing 0.9.3b)
breadboards: 1

parts:
  Part1 = Arduino Nano (Rev3.0)
  Part2 = NRF24L01+ Breakout Board
  DS1 = DS18B20 1-Wire Temperature Sensor [part_number=DS18B20]
  R1 = Resistor [tolerance=±5% resistance=4.7k package=THT]

nets:
  GND: Part1.GND, Part2.GND, DS1.GND
  N1: Part1.D4, DS1.DQ, R1.Pin_1
  N2: Part1.D7, Part2.CE
  N3: Part1.D8, Part2.CS
  N4: Part1.D11/MOSI, Part2.MOSI
  N5: Part1.D12/MISO, Part2.MISO
  5V: Part1.5V, DS1.VDD, R1.Pin_0
  3V3: Part1.3V3, Part2.VCC
  N6: Part1.D13/SCK, Part2.SCK
